// Logisim project RRISC.circ as structural Verilog: 4 circuits, main circuit main
module main (
);

  wire ACC_OUT_IS_JMP, and_1_out, BTN_out, CLK, dipswitch_1_p1, EX, ID, INST_ALU, INST_MEM, INST_MEMWRITE,
       INSTF, not_1_out, or_1_out, RST, WB;
  wire [3:0] ACC_OUT_RX_WB, controlled_buffer_4_out;
  wire [7:0] ALU_OUT_RESULT, controlled_buffer_3_out, IR_q, MEMDATAIN, MEMDATAOUT, R0_ACC, R_CMP,
       regs_1_out_regdata;
  wire [15:0] adder_1_out, MEMADDR, multiplexer_1_out, PC_q, REGS_OUT_MEM;

  and and_1 (and_1_out, INST_MEMWRITE, EX, INST_MEM);
  RAM #(.addrWidth(16), .databus("bidir"), .trigger("high")) ram_1 (
    .addr(MEMADDR), .we(and_1_out), .oe(not_1_out), .data(MEMDATAOUT));
  not not_1 (not_1_out, and_1_out);
  Multiplexer #(.enable("false"), .width(16)) multiplexer_1 (
    .in0(adder_1_out), .in1(REGS_OUT_MEM), .out(multiplexer_1_out), .sel(ACC_OUT_IS_JMP));
  Register #(.width(16)) PC (.D(multiplexer_1_out), .en(1'b1), .clk(WB), .Q(PC_q), .clr(RST));
  Adder #(.width(16)) adder_1 (.a(PC_q), .b(16'h1), .out(adder_1_out));  // open: cin, cout
  assign MEMDATAOUT = and_1_out ? MEMDATAIN : 8'bz;  // Controlled_Buffer controlled_buffer_1
  assign MEMADDR = INSTF ? PC_q : 16'bz;  // Controlled_Buffer controlled_buffer_2
  Register IR (.D(MEMDATAOUT), .en(1'b1), .clk(ID), .Q({IR_q[7:5], INST_MEMWRITE, IR_q[3:0]}), .clr(RST));
  // Probe on MEMDATAOUT
  // DipSwitch #(.number(2)) dipswitch_1: pin names not known; wires that end beside it: dipswitch_1_p1
  // Probe on {IR_q[7:5], INST_MEMWRITE, IR_q[3:0]}
  Button BTN (.out(BTN_out));
  Button BRST (.out(RST));
  or or_1 (or_1_out, EX, WB);
  assign controlled_buffer_3_out = INST_ALU ? ALU_OUT_RESULT : 8'bz;  // Controlled_Buffer controlled_buffer_3
  assign controlled_buffer_4_out = INST_ALU ? ACC_OUT_RX_WB : 4'bz;  // Controlled_Buffer controlled_buffer_4
  nand nand_1 (INST_ALU, IR_q[7], IR_q[6]);
  and u_INST_MEM (INST_MEM, IR_q[5], IR_q[6], IR_q[7]);
  // Probe on controlled_buffer_3_out
  // Probe on IR_q[3:0]
  // Probe on controlled_buffer_4_out
  Controller controller_1 (
    .STEP(dipswitch_1_p1), .BTN(BTN_out), .RST(RST), .INSTF(INSTF), .ID(ID), .EX(EX), .WB(WB), .OUT_CLK(CLK));
  REGS regs_1 (
    .RST(RST), .Data(controlled_buffer_3_out), .CLK(WB), .Write(or_1_out), .Rx_Read(IR_q[3:0]),
    .Rx_Write(controlled_buffer_4_out), .OUT_R0_ACC(R0_ACC), .OUT_REGDATA(regs_1_out_regdata),
    .OUT_CMP(R_CMP), .OUT_MEM(REGS_OUT_MEM));
  // Probe on ALU_OUT_RESULT
  ALU alu_1 (
    .REGDATA(regs_1_out_regdata), .IN_ACC(R0_ACC), .IN_CMP(R_CMP), .IN_IMMEDIATE(IR_q[3:0]),
    .OPCODE({IR_q[7:5], INST_MEMWRITE}), .OUT_RESULT(ALU_OUT_RESULT), .OUT_RX_WB(ACC_OUT_RX_WB),
    .OUT_IS_JMP(ACC_OUT_IS_JMP));
  // Probe on R0_ACC
  // Probe on REGS_OUT_MEM
  assign MEMADDR = WB ? REGS_OUT_MEM : 16'bz;  // Controlled_Buffer controlled_buffer_5
  assign MEMADDR = EX ? REGS_OUT_MEM : 16'bz;  // Controlled_Buffer controlled_buffer_6
  assign MEMADDR = ID ? REGS_OUT_MEM : 16'bz;  // Controlled_Buffer controlled_buffer_7

  // Notes on the sheet:
  //   40MHz = 25ns
  //   30MHz = 33.3ns
  //   20MHz = 50ns
  //   15MHz = 66.6ns
  //   10MHz = 100ns
  //   11ns
  //   <- Expected 16MHz
  //   6ns
  //   Does  one cycle per press
  //   5ns 74as
  //   12ns
endmodule

module ALU (
  input  [7:0] REGDATA,
  input  [7:0] IN_ACC,
  input  [7:0] IN_CMP,
  input  [3:0] IN_IMMEDIATE,
  input  [3:0] OPCODE,
  output [7:0] OUT_RESULT,
  output [3:0] OUT_RX_WB,
  output OUT_IS_JMP
);

  wire and_1_out, comparator_1_eq, comparator_1_gt, comparator_1_lt, multiplexer_3_out, or_1_out, undriven,
       xor_1_out;
  wire [7:0] adder_1_out, and_3_out, bit_extender_1_out, controlled_inverter_1_out, multiplexer_4_out,
       multiplexer_5_out, multiplexer_6_out, multiplexer_7_out, or_2_out, REGORIMM, xor_2_out;

  assign bit_extender_1_out = {{4{1'b0}}, IN_IMMEDIATE};  // Bit_Extender bit_extender_1
  Comparator comparator_1 (.a(IN_ACC), .b(IN_CMP), .gt(comparator_1_gt), .eq(comparator_1_eq), .lt(comparator_1_lt));
  Multiplexer #(.enable("false"), .width(4)) multiplexer_1 (
    .in0(4'b0000), .in1(IN_IMMEDIATE), .out(OUT_RX_WB), .sel(and_1_out));
  and and_1 (and_1_out, OPCODE[0], OPCODE[1], OPCODE[2]);
  or or_1 (or_1_out, REGDATA[0], REGDATA[1], REGDATA[2], REGDATA[3], REGDATA[4], REGDATA[5], REGDATA[6], REGDATA[7]);
  Multiplexer #(.enable("false"), .width(8)) multiplexer_2 (
    .in0(bit_extender_1_out), .in1(REGDATA), .out(REGORIMM), .sel(OPCODE[0]));
  Multiplexer #(.enable("false"), .select(3)) multiplexer_3 (
    .in0(1'b1), .in1(or_1_out), .in2(REGDATA[7]), .in3(comparator_1_gt), .in4(comparator_1_eq),
    .in5(comparator_1_lt), .in6(REGDATA[0]), .in7(undriven), .out(multiplexer_3_out), .sel(IN_IMMEDIATE[3:1]));
  xor xor_1 (xor_1_out, multiplexer_3_out, IN_IMMEDIATE[0]);
  and and_2 (OUT_IS_JMP, OPCODE[0], OPCODE[1], ~OPCODE[2], OPCODE[3], xor_1_out);  // AND_Gate
  Adder adder_1 (.a(IN_ACC), .b(controlled_inverter_1_out), .out(adder_1_out), .cin(OPCODE[0]));  // open: cout
  assign controlled_inverter_1_out = OPCODE[0] ? ~REGORIMM : 8'bz;  // Controlled_Inverter controlled_inverter_1
  assign and_3_out = IN_ACC & REGORIMM;  // AND_Gate and_3, 8 bits wide
  Multiplexer #(.enable("false"), .width(8)) multiplexer_4 (
    .in0(IN_ACC), .in1(REGDATA), .out(multiplexer_4_out), .sel(OPCODE[0]));
  assign or_2_out = IN_ACC | REGORIMM;  // OR_Gate or_2, 8 bits wide
  assign xor_2_out = IN_ACC ^ REGORIMM;  // XOR_Gate xor_2, 8 bits wide
  Multiplexer #(.enable("false"), .width(8)) multiplexer_5 (
    .in0(xor_2_out), .in1({xor_2_out[3:0], xor_2_out[7:4]}), .out(multiplexer_5_out), .sel(OPCODE[0]));
  Multiplexer #(.enable("false"), .width(8)) multiplexer_6 (
    .in0(and_3_out), .in1({and_3_out[3:0], and_3_out[7:4]}), .out(multiplexer_6_out), .sel(OPCODE[0]));
  Multiplexer #(.enable("false"), .width(8)) multiplexer_7 (
    .in0(or_2_out), .in1({or_2_out[3:0], or_2_out[7:4]}), .out(multiplexer_7_out), .sel(OPCODE[0]));
  Multiplexer #(.enable("false"), .select(3), .width(8)) multiplexer_8 (
    .in0(adder_1_out), .in1(adder_1_out), .in2(multiplexer_6_out), .in3(multiplexer_4_out),
    .in4(multiplexer_7_out), .in5(multiplexer_5_out), .in6({IN_ACC[6:0], IN_ACC[7]}), .in7({8{1'b0}}),
    .out(OUT_RESULT), .sel(OPCODE[3:1]));

  // Other names for the same wires on the sheet: IMMEDIATE[3:0] = IN_IMMEDIATE; OPCODE_LSB = OPCODE[0]

  // Notes on the sheet:
  //   Data is register or immediate
  //   If MOV or RB instruction: (DST=IMM) ELSE (DST=ACC)
  //   Conditional Jump
  //   Is Jmp Inst
  //   18.5ns
  //   11ns
  //   Actual ALU Stuff
endmodule

module REGS (
  input  RST,
  input  [7:0] Data,
  input  CLK,
  input  Write,
  input  [3:0] Rx_Read,
  input  [3:0] Rx_Write,
  output [7:0] OUT_R0_ACC,
  output [7:0] OUT_REGDATA,
  output [7:0] OUT_CMP,
  output [15:0] OUT_MEM
);

  wire demultiplexer_1_out0, demultiplexer_1_out1, demultiplexer_1_out2, demultiplexer_1_out3,
       demultiplexer_1_out4, demultiplexer_1_out5, demultiplexer_1_out6, demultiplexer_1_out7,
       demultiplexer_1_out8, demultiplexer_1_out9, demultiplexer_1_out10, demultiplexer_1_out11,
       demultiplexer_1_out12, demultiplexer_1_out13, demultiplexer_1_out14, demultiplexer_1_out15;
  wire [7:0] R1_q, R2_q, R3_q, R4_q, R5_q, R6_q, R7_q, R8_q, R9_q, R10_q, R11_q, R12_q;

  Demultiplexer #(.enable("false"), .select(4)) demultiplexer_1 (
    .out0(demultiplexer_1_out0), .out1(demultiplexer_1_out1), .out2(demultiplexer_1_out2),
    .out3(demultiplexer_1_out3), .out4(demultiplexer_1_out4), .out5(demultiplexer_1_out5),
    .out6(demultiplexer_1_out6), .out7(demultiplexer_1_out7), .out8(demultiplexer_1_out8),
    .out9(demultiplexer_1_out9), .out10(demultiplexer_1_out10), .out11(demultiplexer_1_out11),
    .out12(demultiplexer_1_out12), .out13(demultiplexer_1_out13), .out14(demultiplexer_1_out14),
    .out15(demultiplexer_1_out15), .in(Write), .sel(Rx_Write));
  Register R0_ACC (.D(Data), .en(demultiplexer_1_out0), .clk(CLK), .Q(OUT_R0_ACC), .clr(RST));
  Register R1 (.D(Data), .en(demultiplexer_1_out1), .clk(CLK), .Q(R1_q), .clr(RST));
  Register R2 (.D(Data), .en(demultiplexer_1_out2), .clk(CLK), .Q(R2_q), .clr(RST));
  Register R3 (.D(Data), .en(demultiplexer_1_out3), .clk(CLK), .Q(R3_q), .clr(RST));
  Register R4 (.D(Data), .en(demultiplexer_1_out4), .clk(CLK), .Q(R4_q), .clr(RST));
  Register R5 (.D(Data), .en(demultiplexer_1_out5), .clk(CLK), .Q(R5_q), .clr(RST));
  Register R6 (.D(Data), .en(demultiplexer_1_out6), .clk(CLK), .Q(R6_q), .clr(RST));
  Register R7 (.D(Data), .en(demultiplexer_1_out7), .clk(CLK), .Q(R7_q), .clr(RST));
  Register R8 (.D(Data), .en(demultiplexer_1_out8), .clk(CLK), .Q(R8_q), .clr(RST));
  Register R9 (.D(Data), .en(demultiplexer_1_out9), .clk(CLK), .Q(R9_q), .clr(RST));
  Register R10 (.D(Data), .en(demultiplexer_1_out10), .clk(CLK), .Q(R10_q), .clr(RST));
  Register R11 (.D(Data), .en(demultiplexer_1_out11), .clk(CLK), .Q(R11_q), .clr(RST));
  Register R12 (.D(Data), .en(demultiplexer_1_out12), .clk(CLK), .Q(R12_q), .clr(RST));
  Register R13_MEMIO (.D(Data), .en(demultiplexer_1_out13), .clk(CLK), .Q(OUT_CMP), .clr(RST));
  Register R14_MEML (.D(Data), .en(demultiplexer_1_out14), .clk(CLK), .Q(OUT_MEM[7:0]), .clr(RST));
  Register R15_MEMH (.D(Data), .en(demultiplexer_1_out15), .clk(CLK), .Q(OUT_MEM[15:8]), .clr(RST));
  Multiplexer #(.enable("false"), .select(4), .width(8)) multiplexer_1 (
    .in0(OUT_R0_ACC), .in1(R1_q), .in2(R2_q), .in3(R3_q), .in4(R4_q), .in5(R5_q), .in6(R6_q), .in7(R7_q),
    .in8(R8_q), .in9(R9_q), .in10(R10_q), .in11(R11_q), .in12(R12_q), .in13(OUT_CMP), .in14(OUT_MEM[7:0]),
    .in15(OUT_MEM[15:8]), .out(OUT_REGDATA), .sel(Rx_Read));

  // Notes on the sheet:
  //   6ns
  //   6ns
  //   Is actually 8 16:1 muxes
endmodule

module Controller (
  input  STEP,
  input  BTN,
  input  RST,
  output INSTF,
  output ID,
  output EX,
  output WB,
  output OUT_CLK
);

  wire and_1_out, clock_1_out, demultiplexer_1_out4, or_1_out, or_2_out;
  wire [2:0] adder_1_out, CTR_q;

  or or_1 (or_1_out, ~INSTF, BTN);  // OR_Gate
  or or_2 (or_2_out, RST, demultiplexer_1_out4);
  Clock clock_1 (.out(clock_1_out));
  or or_3 (OUT_CLK, and_1_out, BTN);
  and and_1 (and_1_out, clock_1_out, or_1_out, STEP);
  Register #(.width(3)) CTR (.D(adder_1_out), .en(1'b1), .clk(OUT_CLK), .Q(CTR_q), .clr(or_2_out));
  Demultiplexer #(.enable("false"), .select(3)) demultiplexer_1 (
    .out0(INSTF), .out1(ID), .out2(EX), .out3(WB), .out4(demultiplexer_1_out4), .in(1'b1), .sel(CTR_q));  // open: out5, out6, out7
  Adder #(.width(3)) adder_1 (.a(CTR_q), .b(3'b001), .out(adder_1_out));  // open: cin, cout

  // Notes on the sheet:
  //   This is mostly just a ring counter for the pipeline
endmodule
